# Fritzing sketch HomeAtion_RemotePower_2 (saved by Fritzing 0.8.7b)
perfboards: 1

parts:
  AT328 = atmega328 [package=dip]
  R2 = Resistor [tolerance=±5% resistance=4.7k package=THT]
  Main_switch = DIP SWITCH [package=dipswitch-02]
  R3 = Resistor [tolerance=±5% resistance=1k package=THT]
  POWER_5V = male pin header, 5 pins [form="♂ (male)"]
  C5 = male pin header, 2 pins [form="♂ (male)"]
  C4 = male pin header, 2 pins [form="♂ (male)"]
  LDO_3_3V = male pin header, 3 pins [form="♂ (male)"]
  LED_Power = male pin header, 2 pins [form="♂ (male)"]
  C2 = male pin header, 2 pins [form="♂ (male)"]
  C1 = male pin header, 2 pins [form="♂ (male)"]
  Relay = shrouded pin header, 6 pins [form="♂ (shrouded male)"]
  C3 = male pin header, 3 pins [form="♂ (male)"]
  J4 = female pin header, 4 pins [form="♀ (female)"]
  RF24 = female pin header, 4 pins [form="♀ (female)"]
  Reset = Pushbutton [package="[THT]"]

nets:
  N1: AT328.RESET, R2.Pin_1, Reset.Pin_1, Reset.Pin_2
  N2: AT328.GND#7, C1.pin2
  N3: AT328.D5_(PWM), Relay.pin6
  N4: AT328.D6_(PWM), Relay.pin5
  N5: AT328.D7, Relay.pin4
  N6: AT328.D8, Relay.pin3
  N7: AT328.D9_(PWM), J4.pin3
  N8: AT328.D10_(PWM), RF24.pin3
  N9: AT328.D11_(PWM), RF24.pin2
  N10: AT328.D12, J4.pin1
  N11: AT328.D13, J4.pin2
  N12: R2.Pin_0, C1.pin1
  N13: Main_switch.1, C5.pin1, LDO_3_3V.pin1
  N14: Main_switch.2, C4.pin2, LDO_3_3V.pin3
  N15: Main_switch.3, RF24.pin4
  N16: R3.Pin_0, POWER_5V.pin1
  N17: R3.Pin_1, LED_Power.pin1
  N18: POWER_5V.pin5, C4.pin1, LDO_3_3V.pin2
  N19: C5.pin2, C3.pin1, Reset.Pin_3, Reset.Pin_4
  N20: C2.pin2, Relay.pin1
